# Fritzing sketch wiring (saved by Fritzing 1.0.5)
circuit board: 8.46667cm x 5.64444cm
breadboards: 1

parts:
  Raspberry_Pi1 = Raspberry Pi B+
  LED1 = LED - 5mm [color="Red (633nm)" current=0.030A package="5 mm [THT]"]
  R1 = Resistor [tolerance=±5% power=0.25W resistance=220 package=THT]
  LED2 = LED - 5mm [color="Green (555nm)" current=0.030A package="5 mm [THT]"]
  R2 = Resistor [tolerance=±5% power=0.25W resistance=220 package=THT]
  S1 = Pushbutton [package="[SMD]"]

nets:
  N1: Raspberry_Pi1.GND, LED1.cathode, LED2.cathode, S1.Pin_3, S1.Pin_4
  N2: Raspberry_Pi1.GPIO17, R1.Pin_1
  N3: Raspberry_Pi1.GPIO27, R2.Pin_1
  N4: Raspberry_Pi1.GPIO22, S1.Pin_1, S1.Pin_2
  N5: LED1.anode, R1.Pin_0
  N6: LED2.anode, R2.Pin_0
